// Logisim project CPU.circ as structural Verilog: 1 circuit, main circuit cpu
// RegSegment
module cpu (
);

  wire and_2_out, and_15_out, and_16_out, and_17_out, and_18_out, and_19_out, and_20_out, and_21_out,
       and_22_out, and_23_out, and_24_out, and_26_out, and_27_out, and_28_out, and_29_out, and_30_out,
       and_31_out, and_32_out, and_33_out, and_34_out, and_35_out, and_36_out, clk, demultiplexer_1_out3,
       dipswitch_2_p1, InstructionCache_write, loadToRAM, main_1_out_3, main_2_out_3, main_3_out_3,
       main_4_out_3, main_5_out_3, main_6_out_3, main_7_out_3, main_8_out_3, main_9_out_3, main_10_out_3,
       main_11_out_3, main_12_out_3, main_13_out_3, main_14_out_3, main_15_out_3, main_16_out_3,
       main_17_out_3, main_18_out_3, main_19_out_3, main_20_out_3, main_25_out_3, main_26_out_3,
       main_27_out_3, main_28_out_3, main_29_out_3, main_30_out_3, main_31_out_3, main_32_out_3,
       main_33_out_3, main_34_out_3, main_35_out_3, main_38_out_3, main_39_out_3, main_40_out_3,
       main_41_out_3, main_42_out_3, main_43_out_3, main_44_out_3, main_45_out_3, main_46_out_3,
       main_47_out_3, main_48_out_3, main_49_out_3, main_53_out_3, main_54_out_3, main_55_out_3, mem_wrt,
       not_1_out, not_2_out, not_3_out, not_4_out, not_6_out, not_7_out, not_8_out, not_9_out, not_10_out,
       not_11_out, not_12_out, not_13_out, not_14_out, not_15_out, not_16_out, Operand1Cache_write, or_1_out,
       or_3_out, or_8_out, or_9_out, or_10_out, or_11_out, or_12_out, or_13_out, or_14_out, or_15_out,
       or_16_out, or_17_out, or_18_out, or_19_out, or_20_out, or_21_out, or_23_out, or_24_out, or_29_out,
       R0_write, R1_write, R2_write, R3_write, R4_write, R5_write, R6_write, R7_write, ram_wrt, Reading_op2,
       Registers_highbits, Registers_highbits_req1, Rseg_write, rst, Rtemp_loadFromRAM, Rtemp_loadFromREG,
       segment_enable, undriven;
  wire [1:0] counter_2_q, Rseg_out2;
  wire [7:0] and_1_out, and_5_out, and_6_out, and_7_out, and_8_out, and_9_out, and_12_out,
       bit_extender_2_out, bit_extender_3_out, bit_extender_4_out, bit_extender_5_out, bit_extender_6_out,
       InstructionCache_input8, InstructionCache_out8, InstructionCache_out8LOCK1, InstructionCache_out8SAFE,
       loadToMem_AS8, not_5_out, Operand1Cache_out8, Operand1Cache_out8LOCK1, Operand1Cache_out8SAFE,
       Operand2, or_4_out, or_5_out, ram_1_data, ram_2_data, ram_addr_in8, ram_read_out8, ram_write_in8,
       Reading_op2_ext8, RegisterSelect_read_in8, RegisterSelect_read_out8HIGH, RegisterSelect_read_out8LOW,
       Rtemp_input8, Rtemp_loadFromRAM_AS8, Rtemp_loadFromREG_AS8, Rtemp_loadFromSEG_AS8, segment_enable_AS8,
       undriven_2, undriven_3, undriven_4, undriven_5, undriven_6, undriven_7, undriven_8, undriven_9;
  wire [7:2] Rseg_out8;
  wire [9:0] counter_1_q;
  wire [9:8] ram_addr_in10;
  wire [15:0] R0_out16, R1_out16, R2_out16, R3_out16, R4_out16, R5_out16, R6_out16, R7_out16;

  Clock clock_1 (.out(clk));
  DipSwitch #(.number(2)) dipswitch_1 (.sw2(mem_wrt));  // open: sw1
  Button button_1 (.out(rst));
  Counter #(.max('h3ff), .width(10)) counter_1 (
    .Q(counter_1_q), .up(1'b1), .clk(clk), .clr(rst));  // open: load, D, count, carry
  not not_1 (not_1_out, mem_wrt);
  RAM #(.addrWidth(10), .databus("bidir"), .trigger("high")) ram_1 (
    .addr(counter_1_q), .we(mem_wrt), .oe(not_1_out), .clk(undriven), .data(ram_1_data));
  RAM #(.addrWidth(10), .databus("bidir"), .trigger("high")) ram_2 (
    .addr({ram_addr_in10, ram_addr_in8}), .we(ram_wrt), .oe(not_2_out), .data(ram_2_data));
  not not_2 (not_2_out, ram_wrt);
  not not_3 (not_3_out, mem_wrt);
  assign InstructionCache_input8 = not_3_out ? ram_1_data : 8'bz;  // Controlled_Buffer controlled_buffer_1
  Pull_Resistor pull_resistor_1 (.node(InstructionCache_input8));
  Counter #(.max('h3), .width(2)) counter_2 (
    .Q(counter_2_q), .up(1'b1), .clk(clk), .clr(or_1_out));  // open: load, D, count, carry
  assign Reading_op2_ext8 = {{7{Reading_op2}}, Reading_op2};  // Bit_Extender bit_extender_1
  assign bit_extender_2_out = {{7{Operand1Cache_write}}, Operand1Cache_write};  // Bit_Extender bit_extender_2
  assign and_1_out = bit_extender_2_out & Operand1Cache_out8;  // AND_Gate and_1, 8 bits wide
  assign ram_1_data = mem_wrt ? undriven_2 : 8'bz;  // Controlled_Buffer controlled_buffer_2
  Demultiplexer #(.select(2)) demultiplexer_1 (
    .out0(InstructionCache_write), .out1(Operand1Cache_write), .out2(Reading_op2),
    .out3(demultiplexer_1_out3), .in(1'b1), .sel(counter_2_q));
  and and_2 (and_2_out, counter_2_q[0], counter_2_q[1]);
  or or_1 (or_1_out, and_2_out, rst);
  assign Operand2 = InstructionCache_input8 & Reading_op2_ext8;  // AND_Gate and_3, 8 bits wide
  assign ram_addr_in8 = and_1_out | Operand2;  // OR_Gate or_2, 8 bits wide
  // DipSwitch dipswitch_2: pin names not known; wires that end beside it: dipswitch_2_p1, dipswitch_2_p1, demultiplexer_1_out3
  assign bit_extender_3_out = {{7{Operand1Cache_write}}, Operand1Cache_write};  // Bit_Extender bit_extender_3
  assign ram_2_data = ram_wrt ? ram_write_in8 : 8'bz;  // Controlled_Buffer controlled_buffer_3
  not not_4 (not_4_out, ram_wrt);
  assign ram_read_out8 = not_4_out ? ram_2_data : 8'bz;  // Controlled_Buffer controlled_buffer_4
  assign bit_extender_4_out = {{7{Registers_highbits}}, Registers_highbits};  // Bit_Extender bit_extender_4
  assign InstructionCache_out8LOCK1 = bit_extender_3_out & InstructionCache_out8;  // AND_Gate and_4, 8 bits wide
  or or_3 (or_3_out, Rtemp_loadFromRAM, segment_enable);
  assign and_5_out = RegisterSelect_read_out8HIGH & bit_extender_4_out;  // AND_Gate and_5, 8 bits wide
  assign not_5_out = ~bit_extender_4_out;  // NOT_Gate not_5, 8 bits wide
  assign and_6_out = not_5_out & RegisterSelect_read_out8LOW;  // AND_Gate and_6, 8 bits wide
  assign bit_extender_5_out = {{7{or_3_out}}, or_3_out};  // Bit_Extender bit_extender_5
  assign or_4_out = and_5_out | and_6_out;  // OR_Gate or_4, 8 bits wide
  // LedBar #(.inputtype("row")) ledbar_1: pin names not known; wires that end beside it: ram_write_in8
  assign and_7_out = bit_extender_5_out & ram_read_out8;  // AND_Gate and_7, 8 bits wide
  assign and_8_out = Rtemp_loadFromREG_AS8 & or_4_out;  // AND_Gate and_8, 8 bits wide
  assign and_9_out = Rtemp_loadFromSEG_AS8 & {Rseg_out8, Rseg_out2};  // AND_Gate and_9, 8 bits wide
  // LedBar #(.inputtype("row")) ledbar_2: pin names not known; wires that end beside it: InstructionCache_out8SAFE
  // LedBar #(.inputtype("row")) ledbar_3: pin names not known; wires that end beside it: Operand1Cache_out8SAFE
  // LedBar #(.inputtype("row")) ledbar_4: pin names not known; wires that end beside it: Operand2
  // LedBar #(.inputtype("row")) ledbar_5: pin names not known; wires that end beside it: Operand1Cache_out8LOCK1
  assign bit_extender_6_out = {{7{Operand1Cache_write}}, Operand1Cache_write};  // Bit_Extender bit_extender_6
  assign Operand1Cache_out8LOCK1 = bit_extender_6_out & Operand1Cache_out8;  // AND_Gate and_10, 8 bits wide
  assign or_5_out = and_7_out | and_8_out | and_9_out;  // OR_Gate or_5, 8 bits wide
  all8equal_main main_1 (.in_1(or_5_out), .in_2({8{1'b0}}), .out_3(main_1_out_3));
  assign ram_addr_in10 = Rseg_out2 & {2{segment_enable}};  // AND_Gate and_11, 2 bits wide
  assign and_12_out = Rtemp_loadFromREG_AS8 & Operand1Cache_out8LOCK1;  // AND_Gate and_12, 8 bits wide
  assign Rtemp_input8 = not_6_out ? or_5_out : 8'bz;  // Controlled_Buffer controlled_buffer_5
  not not_6 (not_6_out, main_1_out_3);
  assign Rtemp_input8 = main_1_out_3 ? Operand1Cache_out8LOCK1 : 8'bz;  // Controlled_Buffer controlled_buffer_6
  // LedBar #(.inputtype("row")) ledbar_6: pin names not known; wires that end beside it: InstructionCache_out8LOCK1
  assign RegisterSelect_read_in8 = and_12_out | {8{1'b0}};  // OR_Gate or_6, 8 bits wide
  assign InstructionCache_out8SAFE = Reading_op2_ext8 & InstructionCache_out8;  // AND_Gate and_13, 8 bits wide
  assign Operand1Cache_out8SAFE = Reading_op2_ext8 & Operand1Cache_out8;  // AND_Gate and_14, 8 bits wide
  or or_7 (Registers_highbits, Registers_highbits_req1, 1'b0, 1'b0, 1'b0, 1'b0, 1'b0, 1'b0, 1'b0);
  or or_8 (or_8_out, Registers_highbits, 1'b0);
  and and_15 (and_15_out, InstructionCache_write, 1'b1);
  and and_16 (and_16_out, Operand1Cache_write, 1'b1);
  not not_7 (not_7_out, or_8_out);
  not not_8 (not_8_out, or_8_out);
  not not_9 (not_9_out, or_8_out);
  not not_10 (not_10_out, or_8_out);
  or or_9 (or_9_out, 1'b0, not_7_out);
  and and_17 (and_17_out, or_9_out, R0_write);
  and and_18 (and_18_out, R0_write, or_8_out);
  or or_10 (or_10_out, 1'b0, not_8_out);
  and and_19 (and_19_out, or_10_out, R1_write);
  and and_20 (and_20_out, R1_write, or_8_out);
  or or_11 (or_11_out, 1'b0, not_9_out);
  and and_21 (and_21_out, or_11_out, R2_write);
  and and_22 (and_22_out, R2_write, or_8_out);
  or or_12 (or_12_out, 1'b0, not_10_out);
  and and_23 (and_23_out, or_12_out, R3_write);
  and and_24 (and_24_out, R3_write, or_8_out);
  or or_13 (or_13_out, segment_enable, loadToRAM);
  Register #(.trigger("high")) Reg0_1 (.D(ram_write_in8), .Q(R0_out16[7:0]), .clk(and_17_out));  // open: en, clr
  Register #(.trigger("high")) register_1 (.D(ram_write_in8), .Q(R0_out16[15:8]), .clk(and_18_out));  // open: en, clr
  Register #(.trigger("high")) Reg1_2 (.D(ram_write_in8), .Q(R1_out16[7:0]), .clk(and_19_out));  // open: en, clr
  Register #(.trigger("high")) register_2 (.D(ram_write_in8), .Q(R1_out16[15:8]), .clk(and_20_out));  // open: en, clr
  Register #(.trigger("high")) Reg2_4 (.D(ram_write_in8), .Q(R2_out16[7:0]), .clk(and_21_out));  // open: en, clr
  Register #(.trigger("high")) register_3 (.D(ram_write_in8), .Q(R2_out16[15:8]), .clk(and_22_out));  // open: en, clr
  Register #(.trigger("high")) Reg3_8 (.D(ram_write_in8), .Q(R3_out16[7:0]), .clk(and_23_out));  // open: en, clr
  Register #(.trigger("high")) register_4 (.D(ram_write_in8), .Q(R3_out16[15:8]), .clk(and_24_out));  // open: en, clr
  Register #(.trigger("high")) InstructionCache (
    .D(InstructionCache_input8), .Q(InstructionCache_out8), .clk(and_15_out));  // open: en, clr
  Register #(.trigger("high")) Operand1Cache (
    .D(InstructionCache_input8), .Q(Operand1Cache_out8), .clk(and_16_out));  // open: en, clr
  assign {RegisterSelect_read_out8HIGH, RegisterSelect_read_out8LOW} = RegisterSelect_read_in8[0] ? R0_out16 : 16'bz;  // Controlled_Buffer controlled_buffer_7
  assign {RegisterSelect_read_out8HIGH, RegisterSelect_read_out8LOW} = RegisterSelect_read_in8[1] ? R1_out16 : 16'bz;  // Controlled_Buffer controlled_buffer_8
  assign {RegisterSelect_read_out8HIGH, RegisterSelect_read_out8LOW} = RegisterSelect_read_in8[2] ? R2_out16 : 16'bz;  // Controlled_Buffer controlled_buffer_9
  assign {RegisterSelect_read_out8HIGH, RegisterSelect_read_out8LOW} = RegisterSelect_read_in8[3] ? R3_out16 : 16'bz;  // Controlled_Buffer controlled_buffer_10
  assign {RegisterSelect_read_out8HIGH, RegisterSelect_read_out8LOW} = RegisterSelect_read_in8[4] ? R4_out16 : 16'bz;  // Controlled_Buffer controlled_buffer_11
  assign {RegisterSelect_read_out8HIGH, RegisterSelect_read_out8LOW} = RegisterSelect_read_in8[5] ? R5_out16 : 16'bz;  // Controlled_Buffer controlled_buffer_12
  assign {RegisterSelect_read_out8HIGH, RegisterSelect_read_out8LOW} = RegisterSelect_read_in8[6] ? R6_out16 : 16'bz;  // Controlled_Buffer controlled_buffer_13
  Pull_Resistor pull_resistor_2 (.node({RegisterSelect_read_out8HIGH, RegisterSelect_read_out8LOW}));
  assign {RegisterSelect_read_out8HIGH, RegisterSelect_read_out8LOW} = RegisterSelect_read_in8[7] ? R7_out16 : 16'bz;  // Controlled_Buffer controlled_buffer_14
  and and_25 (ram_wrt, or_13_out, Reading_op2);
  not not_11 (not_11_out, or_14_out);
  or or_14 (or_14_out, Registers_highbits, 1'b0);
  not not_12 (not_12_out, or_14_out);
  not not_13 (not_13_out, or_14_out);
  not not_14 (not_14_out, or_14_out);
  and and_26 (and_26_out, Operand1Cache_write, 1'b1);
  or or_15 (or_15_out, 1'b0, not_11_out);
  and and_27 (and_27_out, or_15_out, R4_write);
  and and_28 (and_28_out, R4_write, or_14_out);
  or or_16 (or_16_out, 1'b0, not_12_out);
  and and_29 (and_29_out, or_16_out, R5_write);
  and and_30 (and_30_out, R5_write, or_14_out);
  or or_17 (or_17_out, 1'b0, not_13_out);
  and and_31 (and_31_out, or_17_out, R6_write);
  and and_32 (and_32_out, R6_write, or_14_out);
  or or_18 (or_18_out, 1'b0, not_14_out);
  and and_33 (and_33_out, or_18_out, R7_write);
  and and_34 (and_34_out, R7_write, or_14_out);
  Register #(.trigger("high")) Reg4 (.D(ram_write_in8), .Q(R4_out16[7:0]), .clk(and_27_out));  // open: en, clr
  Register #(.trigger("high")) register_5 (.D(ram_write_in8), .Q(R4_out16[15:8]), .clk(and_28_out));  // open: en, clr
  Register #(.trigger("high")) Reg5 (.D(ram_write_in8), .Q(R5_out16[7:0]), .clk(and_29_out));  // open: en, clr
  Register #(.trigger("high")) register_6 (.D(ram_write_in8), .Q(R5_out16[15:8]), .clk(and_30_out));  // open: en, clr
  Register #(.trigger("high")) Reg6 (.D(ram_write_in8), .Q(R6_out16[7:0]), .clk(and_31_out));  // open: en, clr
  Register #(.trigger("high")) register_7 (.D(ram_write_in8), .Q(R6_out16[15:8]), .clk(and_32_out));  // open: en, clr
  Register #(.trigger("high")) Reg7 (.D(ram_write_in8), .Q(R7_out16[7:0]), .clk(and_33_out));  // open: en, clr
  Register #(.trigger("high")) register_8 (.D(ram_write_in8), .Q(R7_out16[15:8]), .clk(and_34_out));  // open: en, clr
  Register #(.trigger("high")) SegmentRegister (
    .D(ram_write_in8), .Q({Rseg_out8, Rseg_out2}), .clk(Rseg_write));  // open: en, clr
  Register #(.trigger("high")) TemporaryRegister (
    .D(Rtemp_input8), .Q(ram_write_in8), .clk(and_26_out));  // open: en, clr
  Pull_Resistor pull_resistor_3 (.node({R7_write, R6_write, R5_write, R4_write, R3_write, R2_write, R1_write, R0_write}));
  all8equal_main main_2 (.in_1(8'h1), .in_2(InstructionCache_out8SAFE), .out_3(main_2_out_3));
  all8equal_main main_3 (.in_1(8'h2), .in_2(InstructionCache_out8SAFE), .out_3(main_3_out_3));
  all8equal_main main_4 (.in_1(8'h3), .in_2(InstructionCache_out8SAFE), .out_3(main_4_out_3));
  all8equal_main main_5 (.in_1(8'h4), .in_2(InstructionCache_out8SAFE), .out_3(main_5_out_3));
  all8equal_main main_6 (.in_1(8'h5), .in_2(InstructionCache_out8SAFE), .out_3(main_6_out_3));
  all8equal_main main_7 (.in_1(8'h6), .in_2(InstructionCache_out8SAFE), .out_3(main_7_out_3));
  or or_19 (or_19_out, main_2_out_3, main_3_out_3, main_4_out_3, main_5_out_3, main_6_out_3, main_7_out_3);
  not not_15 (not_15_out, clk);
  and and_35 (and_35_out, or_19_out, not_15_out);
  assign {R7_write, R6_write, R5_write, R4_write, R3_write, R2_write, R1_write, R0_write} = and_35_out ? Operand2 : 8'bz;  // Controlled_Buffer controlled_buffer_15
  not not_16 (not_16_out, clk);
  and and_36 (and_36_out, or_20_out, not_16_out);
  assign {R7_write, R6_write, R5_write, R4_write, R3_write, R2_write, R1_write, R0_write} = and_36_out ? Operand2 : 8'bz;  // Controlled_Buffer controlled_buffer_16
  all8equal_main main_8 (.in_1(8'h7), .in_2(InstructionCache_out8SAFE), .out_3(main_8_out_3));
  all8equal_main main_9 (.in_1(8'h8), .in_2(InstructionCache_out8SAFE), .out_3(main_9_out_3));
  all8equal_main main_10 (.in_1(8'h9), .in_2(InstructionCache_out8SAFE), .out_3(main_10_out_3));
  all8equal_main main_11 (.in_1(8'ha), .in_2(InstructionCache_out8SAFE), .out_3(main_11_out_3));
  all8equal_main main_12 (.in_1(8'hb), .in_2(InstructionCache_out8SAFE), .out_3(main_12_out_3));
  all8equal_main main_13 (.in_1(8'hc), .in_2(InstructionCache_out8SAFE), .out_3(main_13_out_3));
  or or_20 (or_20_out, main_8_out_3, main_9_out_3, main_10_out_3, main_11_out_3, main_12_out_3, main_13_out_3);
  or or_21 (or_21_out, main_14_out_3, main_15_out_3, main_16_out_3, main_17_out_3, main_18_out_3, 1'b0);
  or or_22 (Registers_highbits_req1, or_20_out, or_21_out);
  all8equal_main main_14 (.in_1(InstructionCache_out8LOCK1), .in_2(8'h6), .out_3(main_14_out_3));
  all8equal_main main_15 (.in_1(InstructionCache_out8LOCK1), .in_2(8'hb), .out_3(main_15_out_3));
  all8equal_main main_16 (.in_1(InstructionCache_out8LOCK1), .in_2(8'hf), .out_3(main_16_out_3));
  all8equal_main main_17 (.in_1(InstructionCache_out8LOCK1), .in_2(8'h16), .out_3(main_17_out_3));
  all8equal_main main_18 (.in_1(InstructionCache_out8LOCK1), .in_2(8'h17), .out_3(main_18_out_3));
  all8equal_main main_19 (.in_1(8'h3), .in_2(InstructionCache_out8LOCK1), .out_3(main_19_out_3));
  all8equal_main main_20 (.in_1(8'h9), .in_2(InstructionCache_out8LOCK1), .out_3(main_20_out_3));
  all8equal_main main_21 (.in_1(8'h11), .in_2(InstructionCache_out8LOCK1));  // open: out_3
  all8equal_main main_22 (.in_2(InstructionCache_out8LOCK1));  // open: in_1, out_3
  all8equal_main main_23 (.in_2(InstructionCache_out8LOCK1));  // open: in_1, out_3
  all8equal_main main_24 (.in_2(InstructionCache_out8LOCK1));  // open: in_1, out_3
  or or_23 (or_23_out, main_19_out_3, main_20_out_3, 1'b0, 1'b0, 1'b0, 1'b0);
  or or_24 (or_24_out, main_25_out_3, main_26_out_3, main_27_out_3, 1'b0, 1'b0, 1'b0);
  or or_25 (segment_enable, or_23_out, or_24_out);
  all8equal_main main_25 (.in_1(InstructionCache_out8SAFE), .in_2(8'h13), .out_3(main_25_out_3));
  all8equal_main main_26 (.in_1(InstructionCache_out8SAFE), .in_2(8'h15), .out_3(main_26_out_3));
  all8equal_main main_27 (.in_1(InstructionCache_out8SAFE), .in_2(8'h17), .out_3(main_27_out_3));
  assign segment_enable_AS8 = {{7{segment_enable}}, segment_enable};  // Bit_Extender bit_extender_7
  all8equal_main main_28 (.in_1(8'hd), .in_2(InstructionCache_out8SAFE), .out_3(main_28_out_3));
  all8equal_main main_29 (.in_1(8'he), .in_2(InstructionCache_out8SAFE), .out_3(main_29_out_3));
  all8equal_main main_30 (.in_1(8'hf), .in_2(InstructionCache_out8SAFE), .out_3(main_30_out_3));
  all8equal_main main_31 (.in_1(8'h10), .in_2(InstructionCache_out8SAFE), .out_3(main_31_out_3));
  all8equal_main main_32 (.in_1(8'h11), .in_2(InstructionCache_out8SAFE), .out_3(main_32_out_3));
  or or_26 (Rseg_write, main_28_out_3, main_29_out_3, main_30_out_3, main_31_out_3, main_32_out_3);
  all8equal_main main_33 (.in_1(8'h2), .in_2(InstructionCache_out8LOCK1), .out_3(main_33_out_3));
  all8equal_main main_34 (.in_1(8'h8), .in_2(InstructionCache_out8LOCK1), .out_3(main_34_out_3));
  all8equal_main main_35 (.in_1(8'h10), .in_2(InstructionCache_out8LOCK1), .out_3(main_35_out_3));
  all8equal_main main_36 (.in_1(undriven_3), .in_2(InstructionCache_out8LOCK1));  // open: out_3
  all8equal_main main_37 (.in_1(undriven_4), .in_2(InstructionCache_out8LOCK1));  // open: out_3
  or or_27 (Rtemp_loadFromRAM, main_33_out_3, main_34_out_3, main_35_out_3, 1'b0, 1'b0);
  assign Rtemp_loadFromRAM_AS8 = {{7{Rtemp_loadFromRAM}}, Rtemp_loadFromRAM};  // Bit_Extender bit_extender_8
  all8equal_main main_38 (.in_1(8'h5), .in_2(InstructionCache_out8LOCK1), .out_3(main_38_out_3));
  all8equal_main main_39 (.in_1(8'h6), .in_2(InstructionCache_out8LOCK1), .out_3(main_39_out_3));
  all8equal_main main_40 (.in_1(8'hb), .in_2(InstructionCache_out8LOCK1), .out_3(main_40_out_3));
  all8equal_main main_41 (.in_1(8'hc), .in_2(InstructionCache_out8LOCK1), .out_3(main_41_out_3));
  all8equal_main main_42 (.in_1(8'he), .in_2(InstructionCache_out8LOCK1), .out_3(main_42_out_3));
  all8equal_main main_43 (.in_1(8'hf), .in_2(InstructionCache_out8LOCK1), .out_3(main_43_out_3));
  all8equal_main main_44 (.in_1(8'h14), .in_2(InstructionCache_out8LOCK1), .out_3(main_44_out_3));
  all8equal_main main_45 (.in_1(8'h15), .in_2(InstructionCache_out8LOCK1), .out_3(main_45_out_3));
  all8equal_main main_46 (.in_1(8'h16), .in_2(InstructionCache_out8LOCK1), .out_3(main_46_out_3));
  all8equal_main main_47 (.in_1(8'h17), .in_2(InstructionCache_out8LOCK1), .out_3(main_47_out_3));
  or or_28 (Rtemp_loadFromREG, main_38_out_3, main_39_out_3, main_40_out_3, main_41_out_3, main_42_out_3, main_43_out_3, main_44_out_3, main_45_out_3, main_46_out_3, main_47_out_3);
  assign Rtemp_loadFromREG_AS8 = {{7{Rtemp_loadFromREG}}, Rtemp_loadFromREG};  // Bit_Extender bit_extender_9
  all8equal_main main_48 (.in_1(8'h4), .in_2(InstructionCache_out8LOCK1), .out_3(main_48_out_3));
  all8equal_main main_49 (.in_1(8'ha), .in_2(InstructionCache_out8LOCK1), .out_3(main_49_out_3));
  all8equal_main main_50 (.in_1(undriven_5), .in_2(InstructionCache_out8LOCK1));  // open: out_3
  all8equal_main main_51 (.in_1(undriven_6), .in_2(InstructionCache_out8LOCK1));  // open: out_3
  all8equal_main main_52 (.in_1(undriven_7), .in_2(InstructionCache_out8LOCK1));  // open: out_3
  or or_29 (or_29_out, main_48_out_3, main_49_out_3, 1'b0, 1'b0, 1'b0);
  assign Rtemp_loadFromSEG_AS8 = {{7{or_29_out}}, or_29_out};  // Bit_Extender bit_extender_10
  all8equal_main main_53 (.in_1(8'h12), .in_2(InstructionCache_out8SAFE), .out_3(main_53_out_3));
  all8equal_main main_54 (.in_1(8'h14), .in_2(InstructionCache_out8SAFE), .out_3(main_54_out_3));
  all8equal_main main_55 (.in_1(8'h16), .in_2(InstructionCache_out8SAFE), .out_3(main_55_out_3));
  all8equal_main main_56 (.in_1(undriven_8), .in_2(InstructionCache_out8SAFE));  // open: out_3
  all8equal_main main_57 (.in_1(undriven_9), .in_2(InstructionCache_out8SAFE));  // open: out_3
  or or_30 (loadToRAM, main_53_out_3, main_54_out_3, main_55_out_3, 1'b0, 1'b0);
  assign loadToMem_AS8 = {{7{loadToRAM}}, loadToRAM};  // Bit_Extender bit_extender_11

  // Other names for the same wires on the sheet: memout[7:0] = InstructionCache_input8;
  //   Operand1Cache_input8[7:0] = InstructionCache_input8; ram_addr_in10[7:0] = ram_addr_in8;
  //   Register_write_in8[7:0] = ram_write_in8; Rseg_input8[7:0] = ram_write_in8; Rtemp_out8[7:0] = ram_write_in8;
  //   Reading_instruction = InstructionCache_write;
  //   RegisterSelect_read_out16[15:0] = {RegisterSelect_read_out8HIGH, RegisterSelect_read_out8LOW};
  //   RegisterSelect_write_in8[7:0] = {R7_write, R6_write, R5_write, R4_write, R3_write, R2_write, R1_write, R0_write};
  //   Rseg_out8[1:0] = Rseg_out2; Reading_op1 = Operand1Cache_write; Rtemp_write = Operand1Cache_write

  // Notes on the sheet:
  //   Next ins
  //   1: Code. 0: Exec
  //   Reset
  //   Instructions
  //   MAKE SURE CLK IS 0 at End of Program
  //   mem: memory offset
  //   seg: segment reg
  //   rl/rh: reg low/high
  //   Program Memory
  //   loc: memory + segment
  //   RAM -> temp
  //   Reg -> temp
  //   seg -> temp
  //   immediate-> temp
  //   Memory Addressor
  //   DATA RAM
  //   Memory is always addressed by op1 or op2
  //   Temporary Register loader
  //   implies loadFromRam
  //   Programming Switches
  //   _out8SAFE is only non-zero when currently on operand 2
  //   _out8LOCK1 is only non-zero when currently on operand 1
  //   ASX is 1 bit extended to X bits
  //   8 = least sig
  //   Address type selector
  //   Note that either is zeroed if not on that op
  //   If op1 requests reg read
  //   These are all off if not on operand 2
  //   Instruction
  //   Operand 1
  //   Operand 2 
  //   If no register or mem, use imm8
  //   ALL WRITES SHOULD BE DONE ON CLOCK LOW
  //   Operand 1: only on when on op1
  //   Cache Controller
  //   todo: other requests for reading here
  //   Segment combiner
  //   Highbit selector
  //   Operand 1 LOCK
  //   delete
  //   Operand 2 Executor
  //   It will only actually write if write command is non-zero, so only when ins requested
  //   Registers
  //   TODO: AND WITH CLK
  //   todo, why restricting segment to 2 bits? make it more!
  //   Enable register writing on low bits
  //   chip returns 1 if both entries are identical
  //   Instruction Decoder
  //   Enable register writing on high bits
  //   Enable register reading on high bits
  //   reading
  //   Enable memory segments
  //   writing
  //   Enable segment writing
  //   Enable memory read (DO NOT INCLUDE ANY THAT READ FROM SEG)
  //   Enable register read
  //   Enable segment reading
  //   Enable memory writing (DO NOT INCLUDE ANY THAT WRITE FROM SEG)
endmodule
